# Fritzing sketch Sketch (saved by Fritzing 0.9.2b)
breadboards: 1

parts:
  Composant1 = Arduino Uno (Rev3)
  7_Segment_4_Digit_Display1 = 7-SEGMENT-4DIGIT common anode [part_number="5461BS - 5462BS" package=7-segment-4digit-anode]
  R1 = Resistor [tolerance=±5% resistance=220 package=THT]
  R2 = Resistor [tolerance=±5% resistance=220 package=THT]
  R3 = Resistor [tolerance=±5% resistance=220 package=THT]
  R4 = Resistor [tolerance=±5% resistance=220 package=THT]

nets:
  N1: Composant1.D8, 7_Segment_4_Digit_Display1.pin_4
  N2: Composant1.D9_PWM, 7_Segment_4_Digit_Display1.pin_2
  N3: Composant1.D10_PWM/SS, 7_Segment_4_Digit_Display1.pin_1
  N4: Composant1.D11_PWM/MOSI, 7_Segment_4_Digit_Display1.pin_10
  N5: Composant1.D12/MISO, 7_Segment_4_Digit_Display1.pin_5
  N6: Composant1.D13/SCK, 7_Segment_4_Digit_Display1.pin_3
  N7: Composant1.D2, R1.Pin_0
  N8: Composant1.D3_PWM, R2.Pin_0
  N9: Composant1.D4, R3.Pin_0
  N10: Composant1.D5_PWM, R4.Pin_0
  N11: Composant1.D6_PWM, 7_Segment_4_Digit_Display1.pin_11
  N12: Composant1.D7, 7_Segment_4_Digit_Display1.pin_7
  N13: 7_Segment_4_Digit_Display1.pin_6, R4.Pin_1
  N14: 7_Segment_4_Digit_Display1.pin_8, R3.Pin_1
  N15: 7_Segment_4_Digit_Display1.pin_9, R2.Pin_1
  N16: 7_Segment_4_Digit_Display1.pin_12, R1.Pin_1

custom parts:
  7-SEGMENT-4DIGIT common anode: A 7 Segment 4 Digit common anode display, with decimal points
